# Fritzing sketch wiring_diagram (saved by Fritzing 0.9.3b)

parts:
  Part1 = Arduino Uno (Rev3)
  R1 = Resistor [tolerance=±5% resistance=470 package="0402 [SMD]"]
  NEOPIXEL1 = Neopixel Strip -- Black (60/m)
  U1 = HALL-EFFECT [package=sc70]
  S1 = Taiway 100-SP-X-T1 SPDT Miniature Toggle Switch [part_number=100-SP-X-T1-0-0-B1-M2 package=THT]
  BATT1 = 4xAA Switchable Battery Pack w/Bare Wire
  C1 = Capacitor Polarized [package=cpol-radial-100uf-25v]

nets:
  N1: Part1.D8, U1.OUT
  N2: Part1.D6_PWM, R1.Pin_0
  5V: Part1.5V, NEOPIXEL1.+5V, U1.VCC, S1.L2
  GND: Part1.GND, NEOPIXEL1.GND, U1.GND, BATT1.NEG, C1.-
  N3: R1.Pin_1, NEOPIXEL1.DI
  N4: S1.L1, BATT1.POS, C1.+

custom parts:
  Neopixel Strip -- Black (60/m): Neopixel Strip, Black, 60 pixels per meter.
  4xAA Switchable Battery Pack w/Bare Wire: 4xAA Switchable Battery Pack with Bare Wire connection
